# Fritzing sketch esp01+A_ProMini (saved by Fritzing 0.9.3b)

parts:
  S7 = Round Pushbutton
  S8 = Round Pushbutton
  S9 = Round Pushbutton
  S10 = Round Pushbutton
  S11 = Round Pushbutton
  S12 = Round Pushbutton
  Squix2 = OLED 0.96" 128x64 I2C SSD1306
  Bauteil1 = Arduino Pro Mini (5V)
  Espessif_Serial_Wifi_Modul_1 = ESP8266 ESP01 [part_number=ESP8266 package=THT]

nets:
  N1: S7.leg0, S8.leg0, S9.leg0, Bauteil1.D10
  N2: S10.leg0, Bauteil1.D5
  N3: S11.leg0, Bauteil1.D4
  N4: S12.leg0, Bauteil1.D3
  N5: S12.leg1, Bauteil1.MOSI
  N6: Squix2.SCL, Espessif_Serial_Wifi_Modul_1.GPIO00
  N7: Squix2.SCA, Espessif_Serial_Wifi_Modul_1.GPIO02
  N8: Bauteil1.TXO, Espessif_Serial_Wifi_Modul_1.RXD
  N9: Bauteil1.RXI, Espessif_Serial_Wifi_Modul_1.TXD

notes:
  row 1
  row 2
  colum 3
  colum 2
  colum 1
  data on GPIO2 | clock on GPIO0

custom parts:
  ESP8266 ESP01: Generic WiFi Module based on the ESP8266 with onboard PCB antenna and UART communications
