# Fritzing sketch esp07 (saved by Fritzing 0.9.3b)

parts:
  S1 = Round Pushbutton
  S2 = Round Pushbutton
  S3 = Round Pushbutton
  S4 = Round Pushbutton
  S5 = Round Pushbutton
  S6 = Round Pushbutton
  U1 = ESP8266 WiFi Module [part_number=ESP8266]
  Squix1 = OLED 0.96" 128x64 I2C SSD1306

nets:
  N1: S1.leg0, U1.GPIO_16
  N2: S1.leg1, U1.GPIO_4
  N3: S2.leg0, U1.GPIO_14
  N4: S3.leg0, U1.GPIO_12
  N5: S4.leg0, S5.leg0, S6.leg0, U1.GPIO_15
  N6: U1.GPIO_0, Squix1.SCL
  N7: U1.GPIO_2, Squix1.SCA

notes:
  row 2
  row 1
  colum 1
  colum 2
  colum 3
  data on GPIO2 | clock on GPIO0
